# Fritzing sketch Most Useless Machine (saved by Fritzing 0.5.2b)
breadboards: 1

parts:
  Arduino1 = Arduino
  J1 = Basic Servo
  VCC1 = obsolete Battery
  VCC2 = obsolete Battery
  S1 = Toggle Switch [package=THT]
  R1 = Resistor [resistance=10k package=THT]

nets:
  N1: Arduino1.D9, S1.L2
  N2: Arduino1.D4, J1.pulse
  N3: J1.gnd, R1.Pin_1
  N4: VCC1.+, VCC2.-
  N5: S1.COM, R1.Pin_0

notes:
  Connect 1 side of switch to pin 9 on arduino
  Connect other side to ground through reistor. Without resistor, you will get inconsitant results.
  A 1K to 10K should work great
  You can use a 9 volt battery with a 7205 v regulator, however you will loose a lot of battery life through heat.
  I had a 4 port AA battery holder.
  While it is 6v and technically too high, I haven't had any problems.
  You can add anything else you want.
  leds, Speakers, Vibrating motor, Squirtgun?
